// Logisim project taxi_meter.circ as structural Verilog: 9 circuits, main circuit distance calculator
module distance_calculator (
  input  Start_Stop_Ride,
  input  [11:0] \input ,
  input  Reset,
  output [11:0] out_4,
  output [3:0] out_5,
  output [11:0] No_Of_Half_Kms
);

  wire comparator_1_eq;
  wire [11:0] divider_1_rem;

  Comparator #(.width(12)) comparator_1 (.a(\input ), .b(12'h96), .eq(comparator_1_eq));  // open: gt, lt
  Counter #(.width(12), .max('hfff)) NoOfHalfKms (
    .count(Start_Stop_Ride), .Q(No_Of_Half_Kms), .clk(comparator_1_eq), .clr(Reset));  // open: load, D, carry
  Divider #(.width(12)) divider_1 (.a(No_Of_Half_Kms), .b(12'h2), .out(out_4), .rem(divider_1_rem));  // open: upper
  Multiplexer #(.width(4)) multiplexer_1 (
    .in0(4'b0000), .in1(4'b0101), .out(out_5), .sel(divider_1_rem[0]));  // open: en

  // Notes on the sheet:
  //   Display No Of Kms Travelled
  //   Display Dec Part Of Kms Travelled
endmodule

module binarytodecimaldisp (
  input  [11:0] INPUT,
  output [3:0] MSB_A,
  output [3:0] B,
  output [3:0] C,
  output [3:0] LSB_D
);

  wire add3method_1_b_2, add3method_1_c_2, add3method_1_lsb_d_2, add3method_1_msb_a_2, add3method_2_b_2,
       add3method_2_c_2, add3method_2_lsb_d_2, add3method_2_msb_a_2, add3method_3_b_2, add3method_3_c_2,
       add3method_3_lsb_d_2, add3method_3_msb_a_2, add3method_4_b_2, add3method_4_c_2, add3method_4_lsb_d_2,
       add3method_4_msb_a_2, add3method_5_b_2, add3method_5_c_2, add3method_5_lsb_d_2, add3method_5_msb_a_2,
       add3method_6_b_2, add3method_6_c_2, add3method_6_lsb_d_2, add3method_6_msb_a_2, add3method_7_b_2,
       add3method_7_c_2, add3method_7_lsb_d_2, add3method_7_msb_a_2, add3method_8_b_2, add3method_8_c_2,
       add3method_8_lsb_d_2, add3method_8_msb_a_2, add3method_9_b_2, add3method_9_c_2, add3method_9_lsb_d_2,
       add3method_9_msb_a_2, add3method_10_b_2, add3method_10_c_2, add3method_10_lsb_d_2, add3method_11_b_2,
       add3method_11_c_2, add3method_11_lsb_d_2, add3method_12_b_2, add3method_12_c_2, add3method_12_lsb_d_2,
       add3method_12_msb_a_2, add3method_15_b_2, add3method_15_c_2, add3method_15_lsb_d_2,
       add3method_15_msb_a_2, add3method_16_b_2, add3method_16_c_2, add3method_16_lsb_d_2,
       add3method_16_msb_a_2, add3method_17_b_2, add3method_17_c_2, add3method_17_lsb_d_2,
       add3method_17_msb_a_2;

  add3method add3method_1 (
    .MSB_A(1'b0), .B(INPUT[11]), .C(INPUT[10]), .LSB_D(INPUT[9]), .MSB_A_2(add3method_1_msb_a_2),
    .B_2(add3method_1_b_2), .C_2(add3method_1_c_2), .LSB_D_2(add3method_1_lsb_d_2));
  add3method add3method_2 (
    .MSB_A(add3method_1_b_2), .B(add3method_1_c_2), .C(add3method_1_lsb_d_2), .LSB_D(INPUT[8]),
    .MSB_A_2(add3method_2_msb_a_2), .B_2(add3method_2_b_2), .C_2(add3method_2_c_2),
    .LSB_D_2(add3method_2_lsb_d_2));
  add3method add3method_3 (
    .MSB_A(add3method_2_b_2), .B(add3method_2_c_2), .C(add3method_2_lsb_d_2), .LSB_D(INPUT[7]),
    .MSB_A_2(add3method_3_msb_a_2), .B_2(add3method_3_b_2), .C_2(add3method_3_c_2),
    .LSB_D_2(add3method_3_lsb_d_2));
  add3method add3method_4 (
    .MSB_A(add3method_3_b_2), .B(add3method_3_c_2), .C(add3method_3_lsb_d_2), .LSB_D(INPUT[6]),
    .MSB_A_2(add3method_4_msb_a_2), .B_2(add3method_4_b_2), .C_2(add3method_4_c_2),
    .LSB_D_2(add3method_4_lsb_d_2));
  add3method add3method_5 (
    .MSB_A(1'b0), .B(add3method_1_msb_a_2), .C(add3method_2_msb_a_2), .LSB_D(add3method_3_msb_a_2),
    .MSB_A_2(add3method_5_msb_a_2), .B_2(add3method_5_b_2), .C_2(add3method_5_c_2),
    .LSB_D_2(add3method_5_lsb_d_2));
  add3method add3method_6 (
    .MSB_A(add3method_5_b_2), .B(add3method_5_c_2), .C(add3method_5_lsb_d_2), .LSB_D(add3method_4_msb_a_2),
    .MSB_A_2(add3method_6_msb_a_2), .B_2(add3method_6_b_2), .C_2(add3method_6_c_2),
    .LSB_D_2(add3method_6_lsb_d_2));
  add3method add3method_7 (
    .MSB_A(add3method_4_b_2), .B(add3method_4_c_2), .C(add3method_4_lsb_d_2), .LSB_D(INPUT[5]),
    .MSB_A_2(add3method_7_msb_a_2), .B_2(add3method_7_b_2), .C_2(add3method_7_c_2),
    .LSB_D_2(add3method_7_lsb_d_2));
  add3method add3method_8 (
    .MSB_A(add3method_6_b_2), .B(add3method_6_c_2), .C(add3method_6_lsb_d_2), .LSB_D(add3method_7_msb_a_2),
    .MSB_A_2(add3method_8_msb_a_2), .B_2(add3method_8_b_2), .C_2(add3method_8_c_2),
    .LSB_D_2(add3method_8_lsb_d_2));
  add3method add3method_9 (
    .MSB_A(add3method_8_b_2), .B(add3method_8_c_2), .C(add3method_8_lsb_d_2), .LSB_D(add3method_15_msb_a_2),
    .MSB_A_2(add3method_9_msb_a_2), .B_2(add3method_9_b_2), .C_2(add3method_9_c_2),
    .LSB_D_2(add3method_9_lsb_d_2));
  add3method add3method_10 (
    .MSB_A(1'b0), .B(add3method_5_msb_a_2), .C(add3method_6_msb_a_2), .LSB_D(add3method_8_msb_a_2),
    .MSB_A_2(MSB_A[2]), .B_2(add3method_10_b_2), .C_2(add3method_10_c_2), .LSB_D_2(add3method_10_lsb_d_2));
  add3method add3method_11 (
    .MSB_A(add3method_10_b_2), .B(add3method_10_c_2), .C(add3method_10_lsb_d_2),
    .LSB_D(add3method_9_msb_a_2), .MSB_A_2(MSB_A[1]), .B_2(add3method_11_b_2), .C_2(add3method_11_c_2),
    .LSB_D_2(add3method_11_lsb_d_2));
  add3method add3method_12 (
    .MSB_A(add3method_9_b_2), .B(add3method_9_c_2), .C(add3method_9_lsb_d_2), .LSB_D(add3method_16_msb_a_2),
    .MSB_A_2(add3method_12_msb_a_2), .B_2(add3method_12_b_2), .C_2(add3method_12_c_2),
    .LSB_D_2(add3method_12_lsb_d_2));
  add3method add3method_13 (
    .MSB_A(add3method_12_b_2), .B(add3method_12_c_2), .C(add3method_12_lsb_d_2),
    .LSB_D(add3method_17_msb_a_2), .MSB_A_2(B[0]), .B_2(C[3]), .C_2(C[2]), .LSB_D_2(C[1]));
  add3method add3method_14 (
    .MSB_A(add3method_11_b_2), .B(add3method_11_c_2), .C(add3method_11_lsb_d_2),
    .LSB_D(add3method_12_msb_a_2), .MSB_A_2(MSB_A[0]), .B_2(B[3]), .C_2(B[2]), .LSB_D_2(B[1]));
  add3method add3method_15 (
    .MSB_A(add3method_7_b_2), .B(add3method_7_c_2), .C(add3method_7_lsb_d_2), .LSB_D(INPUT[4]),
    .MSB_A_2(add3method_15_msb_a_2), .B_2(add3method_15_b_2), .C_2(add3method_15_c_2),
    .LSB_D_2(add3method_15_lsb_d_2));
  add3method add3method_16 (
    .MSB_A(add3method_15_b_2), .B(add3method_15_c_2), .C(add3method_15_lsb_d_2), .LSB_D(INPUT[3]),
    .MSB_A_2(add3method_16_msb_a_2), .B_2(add3method_16_b_2), .C_2(add3method_16_c_2),
    .LSB_D_2(add3method_16_lsb_d_2));
  add3method add3method_17 (
    .MSB_A(add3method_16_b_2), .B(add3method_16_c_2), .C(add3method_16_lsb_d_2), .LSB_D(INPUT[2]),
    .MSB_A_2(add3method_17_msb_a_2), .B_2(add3method_17_b_2), .C_2(add3method_17_c_2),
    .LSB_D_2(add3method_17_lsb_d_2));
  add3method add3method_18 (
    .MSB_A(add3method_17_b_2), .B(add3method_17_c_2), .C(add3method_17_lsb_d_2), .LSB_D(INPUT[1]),
    .MSB_A_2(C[0]), .B_2(LSB_D[3]), .C_2(LSB_D[2]), .LSB_D_2(LSB_D[1]));

  assign LSB_D[0] = INPUT[0];
  assign MSB_A[3] = 1'b0;
endmodule

module add3method (
  input  MSB_A,
  input  B,
  input  C,
  input  LSB_D,
  output MSB_A_2,
  output B_2,
  output C_2,
  output LSB_D_2
);

  wire [1:1] comparator_1_gt;

  Comparator #(.width(4), .mode("unsigned")) comparator_1 (
    .a({MSB_A, B, C, LSB_D}), .b(4'b0100), .gt(comparator_1_gt[1]));  // open: eq, lt
  Adder #(.width(4)) adder_1 (
    .a({MSB_A, B, C, LSB_D}), .b({2'b00, {2{comparator_1_gt[1]}}}), .out({MSB_A_2, B_2, C_2, LSB_D_2}));  // open: cin, cout

  // Notes on the sheet:
  //   INPUT
  //   COMPARATOR
  //   ADDER
  //   OUTPUT
endmodule

module fare (
  input  [11:0] No_of_Half_kms,
  input  [11:0] Fare_Input,
  input  [11:0] Waiting_Time_Input,
  output [11:0] Total_Fare
);

  wire [11:0] multiplier_1_out;

  Multiplier #(.width(12)) multiplier_1 (
    .a(No_of_Half_kms), .b(Fare_Input), .out(multiplier_1_out));  // open: cin, cout
  Adder #(.width(12)) adder_1 (.a(multiplier_1_out), .b(Waiting_Time_Input), .out(Total_Fare));  // open: cin, cout

  // Notes on the sheet:
  //   Fare price*5
  //   Waiting time price
  //   HalfKm*Price
  //   Fare Price
endmodule

module waitingtimeblock (
  input  Start_Stop_Waiting,
  input  Reset_Waiting,
  output [11:0] Waiting_Time_Price,
  output ToggleOutput
);

  wire clock_1_out, j_k_ff_1_q;
  wire [11:0] counter_1_q, register_1_q;

  J_K_Flip_Flop j_k_ff_1 (
    .J(1'b1), .clk(Start_Stop_Waiting), .K(j_k_ff_1_q), .Q(j_k_ff_1_q));  // open: Qn, preset, en, reset
  not not_1 (ToggleOutput, j_k_ff_1_q);
  Counter #(.width(12), .max('hfff)) counter_1 (
    .D({12{1'b0}}), .count(j_k_ff_1_q), .Q(counter_1_q), .clk(clock_1_out), .clr(ToggleOutput));  // open: load, carry
  Clock #(.highDuration(1000), .lowDuration(1000)) clock_1 (.out(clock_1_out));
  Register #(.width(12)) register_1 (
    .D(counter_1_q), .en(j_k_ff_1_q), .Q(register_1_q), .clk(clock_1_out), .clr(Reset_Waiting));
  Multiplier #(.width(12)) multiplier_1 (.a(register_1_q), .b(12'h1), .out(Waiting_Time_Price));  // open: cin, cout

  // Notes on the sheet:
  //   Waiting TIme counter
  //   Register to store waiting time price
endmodule

module faredisplay (
  input  Fare_Input,
  output [11:0] Fare_for_Half_km,
  output [3:0] Fare_Per_Km_digit_1,
  output [3:0] Fare_Per_Km_digit_2
);

  wire [11:4] counter_1_q;

  Counter #(.width(12), .max('h5)) counter_1 (
    .Q({counter_1_q, Fare_Per_Km_digit_1}), .clk(Fare_Input));  // open: load, D, count, carry, clr
  Multiplier #(.width(12)) multiplier_1 (
    .a({counter_1_q, Fare_Per_Km_digit_1}), .b(12'h5), .out(Fare_for_Half_km));  // open: cin, cout

  assign Fare_Per_Km_digit_2 = 4'b0000;
endmodule

module inputblock (
  input  Start_Stop_Ride,
  input  Reset,
  output Start_Stop,
  output [11:0] CircInput,
  output ResetOutput
);

  J_K_Flip_Flop j_k_ff_1 (
    .J(1'b1), .clk(Start_Stop_Ride), .K(Start_Stop), .Q(Start_Stop));  // open: Qn, preset, en, reset
  J_K_Flip_Flop j_k_ff_2 (.J(1'b1), .clk(Reset), .K(ResetOutput), .Q(ResetOutput));  // open: Qn, preset, en, reset
  mod3 mod3_1 (.out_2(CircInput), .count(Start_Stop));

  // Notes on the sheet:
  //   Count rotations
endmodule

module main (
);

  wire button_1_out, button_2_out, button_3_out, button_4_out, inputblock_1_resetoutput,
       inputblock_1_start_stop, not_1_out, waitingtimeblock_1_toggleoutput;
  wire [3:0] binarytodecimaldisp_1_b, binarytodecimaldisp_1_c, binarytodecimaldisp_1_lsb_d,
       binarytodecimaldisp_1_msb_a, binarytodecimaldisp_2_b, binarytodecimaldisp_2_c,
       binarytodecimaldisp_2_lsb_d, binarytodecimaldisp_2_msb_a, distance_calculator_1_out_5,
       faredisplay_1_fare_per_km_digit_1, faredisplay_1_fare_per_km_digit_2;
  wire [11:0] distance_calculator_1_no_of_half_kms, distance_calculator_1_out_4, fare_1_total_fare,
       faredisplay_1_fare_for_half_km, inputblock_1_circinput, waitingtimeblock_1_waiting_time_price;

  Button button_1 (.out(button_1_out));
  Button button_2 (.out(button_2_out));
  Button button_3 (.out(button_3_out));
  LED StartRide (.in(inputblock_1_start_stop));
  LED Reset (.in(inputblock_1_resetoutput));
  LED WaitingTime (.in(not_1_out));
  Button button_4 (.out(button_4_out));
  not not_1 (not_1_out, waitingtimeblock_1_toggleoutput);
  Hex_Digit_Display hex_digit_display_1 (.value(faredisplay_1_fare_per_km_digit_1));  // open: dp
  Hex_Digit_Display hex_digit_display_2 (.value(faredisplay_1_fare_per_km_digit_2));  // open: dp
  faredisplay faredisplay_1 (
    .Fare_Per_Km_digit_2(faredisplay_1_fare_per_km_digit_2), .Fare_Input(button_1_out),
    .Fare_Per_Km_digit_1(faredisplay_1_fare_per_km_digit_1), .Fare_for_Half_km(faredisplay_1_fare_for_half_km));
  inputblock inputblock_1 (
    .CircInput(inputblock_1_circinput), .Start_Stop_Ride(button_2_out), .Reset(button_3_out),
    .ResetOutput(inputblock_1_resetoutput), .Start_Stop(inputblock_1_start_stop));
  Hex_Digit_Display hex_digit_display_3 (.value(binarytodecimaldisp_1_b));  // open: dp
  Hex_Digit_Display hex_digit_display_4 (.value(binarytodecimaldisp_1_msb_a));  // open: dp
  Hex_Digit_Display hex_digit_display_5 (.value(binarytodecimaldisp_1_c));  // open: dp
  Hex_Digit_Display hex_digit_display_6 (.value(binarytodecimaldisp_1_lsb_d), .dp(1'b1));
  binarytodecimaldisp binarytodecimaldisp_1 (
    .INPUT(distance_calculator_1_out_4), .MSB_A(binarytodecimaldisp_1_msb_a), .B(binarytodecimaldisp_1_b),
    .C(binarytodecimaldisp_1_c), .LSB_D(binarytodecimaldisp_1_lsb_d));
  waitingtimeblock waitingtimeblock_1 (
    .Waiting_Time_Price(waitingtimeblock_1_waiting_time_price), .Reset_Waiting(inputblock_1_resetoutput),
    .Start_Stop_Waiting(button_4_out), .ToggleOutput(waitingtimeblock_1_toggleoutput));
  Hex_Digit_Display hex_digit_display_7 (.value(distance_calculator_1_out_5));  // open: dp
  distance_calculator distance_calculator_1 (
    .out_4(distance_calculator_1_out_4), .out_5(distance_calculator_1_out_5),
    .No_Of_Half_Kms(distance_calculator_1_no_of_half_kms), .Reset(inputblock_1_resetoutput),
    .\input (inputblock_1_circinput), .Start_Stop_Ride(waitingtimeblock_1_toggleoutput));
  fare fare_1 (
    .No_of_Half_kms(distance_calculator_1_no_of_half_kms),
    .Waiting_Time_Input(waitingtimeblock_1_waiting_time_price), .Total_Fare(fare_1_total_fare),
    .Fare_Input(faredisplay_1_fare_for_half_km));
  Hex_Digit_Display hex_digit_display_8 (.value(binarytodecimaldisp_2_msb_a));  // open: dp
  Hex_Digit_Display hex_digit_display_9 (.value(binarytodecimaldisp_2_c));  // open: dp
  Hex_Digit_Display hex_digit_display_10 (.value(binarytodecimaldisp_2_b));  // open: dp
  Hex_Digit_Display hex_digit_display_11 (.value(binarytodecimaldisp_2_lsb_d));  // open: dp
  binarytodecimaldisp binarytodecimaldisp_2 (
    .INPUT(fare_1_total_fare), .MSB_A(binarytodecimaldisp_2_msb_a), .B(binarytodecimaldisp_2_b),
    .C(binarytodecimaldisp_2_c), .LSB_D(binarytodecimaldisp_2_lsb_d));

  // Notes on the sheet:
  //   Rs
  //   Fare per KM
  //   Total Distance
  //   KM
  //   Rs
  //   Total Fare
endmodule

module mod3 (
  input  count,
  output [11:0] out_2
);

  wire and_1_out, and_2_out, and_3_out, and_4_out, clock_1_out;

  Counter #(.width(12), .max('hfff)) counter_1 (
    .count(count), .Q(out_2), .clk(clock_1_out), .clr(and_4_out));  // open: load, D, carry
  Clock clock_1 (.out(clock_1_out));
  and and_1 (and_1_out, out_2[5], ~out_2[4]);  // AND_Gate
  and and_2 (and_2_out, ~out_2[1], out_2[0]);  // AND_Gate
  and and_3 (and_3_out, and_1_out, out_2[3], out_2[2], and_2_out);
  and and_4 (and_4_out, out_2[8], and_3_out, out_2[0]);

  // Notes on the sheet:
  //   MOD 300 Counter
endmodule
